# Fritzing sketch HC-SRF04 (saved by Fritzing 0.9.4)
breadboards: 1

parts:
  Mod1 = Raspberry Pi Pico W
  HC-SR04_Sensor_1 = HC-SR04 Ultrasonic Distance Sensor
  LED1 = LED - 3mm [color="Green (555nm)" package="3 mm [THT]"]
  R1 = Resistor [tolerance=±5% resistance=56 package=THT]

nets:
  N1: Mod1.pin_3, Mod1.pin_8, Mod1.pin_13, Mod1.pin_18, Mod1.pin_23, Mod1.pin_28, Mod1.pin_33, Mod1.pin_38, HC-SR04_Sensor_1.GND, LED1.anode
  N2: Mod1.pin_4, HC-SR04_Sensor_1.TRIG
  N3: Mod1.pin_5, HC-SR04_Sensor_1.ECHO
  N4: Mod1.pin_20, R1.Pin_0
  N5: Mod1.pin_36, HC-SR04_Sensor_1.VCC
  N6: LED1.cathode, R1.Pin_1

custom parts:
  Raspberry Pi Pico W: Raspberry Pi Pico W. Based around the RP2040 microcontroller the Pico W is a low cost microcontroller device bringing Raspberry Pi quality, cost, and easy of use to the microcontroller space. The areas marked KEEPOUT in pcb silkscreen should not have traces running through them to avoid shorts on a soldered in module!
